# Fritzing sketch Control Circuit (saved by Fritzing 0.9.3b)
circuit board: 8.46667cm x 5.64444cm
breadboards: 3

parts:
  U1 = Mini-360 DC-DC Buck converter [package=THT]
  S1 = Toggle Switch [package=THT]
  U2 = NodeMCU V3.0
  S2 = Pushbutton [package="[SMD]"]
  R1 = Resistor [tolerance=±5% resistance=10k package="2512 [SMD]"]
  R2 = Resistor [tolerance=±5% resistance=10k package="2512 [SMD]"]
  S3 = Pushbutton [package="[SMD]"]
  LED1 = smd LED [color="White (4500K)" package="1206 [SMD]"]
  R3 = Resistor [tolerance=±5% resistance=2.2k package="2512 [SMD]"]
  R4 = Resistor [tolerance=±5% resistance=10k package="2512 [SMD]"]
  S5 = Pushbutton [package="[SMD]"]
  U3 = 74HC595 [package="DIP16 [THT]"]
  J1 = female pin header, 4 pins [form="♀ (female)"]
  J2 = female pin header, 4 pins [form="♀ (female)"]
  J3 = female pin header, 4 pins [form="♀ (female)"]
  U4 = 74HC595 [package="DIP16 [THT]"]
  J5 = female pin header, 2 pins [form="♀ (female)"]
  J6 = female pin header, 2 pins [form="♀ (female)"]

nets:
  GND: U1.IN-, U1.OUT-, U2.GND, R3.Pin_0, R4.Pin_0, U3.GND, U3.OE, U4.GND, U4.OE, J5.pin2, J6.pin2
  N1: S1.COM, J5.pin1, J6.pin1
  N2: U2.D0, R4.Pin_1, S5.Pin_1, S5.Pin_2
  N3: U2.D1, LED1.anode
  N4: U2.D2, U3.ST_CP, U4.ST_CP
  VCC: U2.3V3, S2.Pin_3, S2.Pin_4, S3.Pin_3, S3.Pin_4, S5.Pin_3, S5.Pin_4, U3.MR, U3.VCC, U4.MR, U4.VCC
  N5: U2.D5, U3.SH_CP, U4.SH_CP
  N6: U2.D6, R1.Pin_0, R2.Pin_0, R2.Pin_1, S3.Pin_1, S3.Pin_2
  N7: U2.D7, U3.DS
  N8: U2.D8, S2.Pin_1, S2.Pin_2, R1.Pin_1
  N9: U2.VU, U3.Q1
  N10: LED1.cathode, R3.Pin_1
  N11: U3.Q2, J1.pin3
  N12: U3.Q3, J1.pin4
  N13: U3.Q4, J2.pin1
  N14: U3.Q5, J2.pin2
  N15: U3.Q6, J2.pin3
  N16: U3.Q7, J2.pin4
  N17: U3.Q7', U4.DS
  N18: U3.Q0, J1.pin1
  N19: J3.pin1, U4.Q0
  N20: J3.pin2, U4.Q1
  N21: J3.pin3, U4.Q2
  N22: J3.pin4, U4.Q3

notes:
  +12V
  GND

custom parts:
  Mini-360 DC-DC Buck converter: Mini-360 DC-DC Buck converter. Tiny buck step down voltage converter, input voltage 4.75 to 23V output 1 to 17V adjustable. Available from ebay and the like.
  NodeMCU V3.0: ESP8266 based NodeMCU
