# Fritzing sketch Blue Button LED Switching Circuit (saved by Fritzing 0.9.3b)
breadboards: 1

parts:
  Blue_Button_LED = LED - 3mm [color="Blue (525nm)" package="3 mm [THT]"]
  R1 = Resistor [tolerance=±5% resistance=100k package="0805 [SMD]"]
  12_V = female pin header, 1 pin [form="♀ (female)"]
  Q1 = TRANSISTOR_NPN [package=to-92]
  to_D1 = female pin header, 1 pin [form="♀ (female)"]
  R2 = Resistor [tolerance=±5% resistance=200k package="0805 [SMD]"]

nets:
  N1: Blue_Button_LED.cathode, Q1.C
  N2: Blue_Button_LED.anode, R1.Pin_1
  N3: R1.Pin_0, 12_V.pin1
  GND: Q1.E
  N4: Q1.B, R2.Pin_1
  N5: to_D1.pin1, R2.Pin_0

notes:
  D1 normally HIGH, LOW to flash
